// Logisim project partie1.circ as structural Verilog: 1 circuit, main circuit main
module main (
  input  r0,
  input  a1,
  input  b1,
  output s1,
  output r1
);

  wire and_1_out, and_2_out, clock_1_out, decoder_1_out0, decoder_1_out1, decoder_1_out2, decoder_1_out3,
       decoder_1_out4, decoder_1_out5, decoder_1_out6, decoder_1_out7, xor_1_out;
  wire [2:0] counter_1_q;

  xor xor_1 (xor_1_out, a1, b1);
  and and_1 (and_1_out, b1, a1);
  Counter #(.width(3), .max('h7)) counter_1 (.Q(counter_1_q), .clk(clock_1_out));  // open: load, D, count, carry, clr
  Clock clock_1 (.out(clock_1_out));
  ExactlyOne xor_2 (.out(s1), .in0(r0), .in1(r0), .in3(xor_1_out));
  and and_2 (and_2_out, r0, xor_1_out);
  LED led_1 (.in(decoder_1_out7));
  LED led_2 (.in(decoder_1_out6));
  LED led_3 (.in(decoder_1_out5));
  or or_1 (r1, and_2_out, and_1_out);
  Decoder #(.select(3)) decoder_1 (
    .out0(decoder_1_out0), .out1(decoder_1_out1), .out2(decoder_1_out2), .out3(decoder_1_out3),
    .out4(decoder_1_out4), .out5(decoder_1_out5), .out6(decoder_1_out6), .out7(decoder_1_out7),
    .sel(counter_1_q));  // open: en
  LED led_4 (.in(decoder_1_out0));
  LED led_5 (.in(decoder_1_out1));
  LED led_6 (.in(decoder_1_out2));
  LED led_7 (.in(decoder_1_out3));
  LED led_8 (.in(decoder_1_out4));
endmodule
