// Logisim project feu1.circ as structural Verilog: 1 circuit, main circuit main
module main (
);

  wire and_1_out, and_2_out, and_3_out, and_4_out, clock_1_out, not_1_out, not_2_out;
  wire [1:0] counter_1_q;

  Clock clock_1 (.out(clock_1_out));
  Counter #(.width(2), .max('h3)) counter_1 (.Q(counter_1_q), .clk(clock_1_out));  // open: load, D, count, carry, clr
  not not_1 (not_1_out, counter_1_q[0]);
  not not_2 (not_2_out, counter_1_q[1]);
  and and_1 (and_1_out, counter_1_q[0], not_2_out);
  LED led_1 (.in(counter_1_q[1]));
  LED led_2 (.in(and_1_out));
  LED led_3 (.in(and_2_out));
  and and_2 (and_2_out, not_1_out, not_2_out);
  and and_3 (and_3_out, counter_1_q[0], counter_1_q[1]);
  and and_4 (and_4_out, counter_1_q[1], not_1_out);
  LED led_4 (.in(not_2_out));
  LED led_5 (.in(and_3_out));
  LED led_6 (.in(and_4_out));
endmodule
