// Logisim project feu2.circ as structural Verilog: 1 circuit, main circuit main
module main (
);

  wire and_1_out, and_2_out, and_3_out, and_4_out, and_5_out, clock_1_out, not_1_out, not_2_out, not_4_out;
  wire [2:0] counter_1_q;

  and and_1 (and_1_out, counter_1_q[0], counter_1_q[1]);
  Clock clock_1 (.out(clock_1_out));
  not not_1 (not_1_out, and_1_out);
  Counter #(.width(3), .max('h7)) counter_1 (.Q(counter_1_q), .clk(clock_1_out));  // open: load, D, count, carry, clr
  and and_2 (and_2_out, not_4_out, not_1_out);
  and and_3 (and_3_out, not_1_out, counter_1_q[2]);
  and and_4 (and_4_out, not_4_out, counter_1_q[0], counter_1_q[1]);
  not not_2 (not_2_out, counter_1_q[1]);
  // NOT_Gate not_3 has open pins: in=counter_1_q[0], out=open
  not not_4 (not_4_out, counter_1_q[2]);
  LED led_1 (.in(counter_1_q[2]));
  LED led_2 (.in(and_4_out));
  LED led_3 (.in(and_2_out));
  and and_5 (and_5_out, counter_1_q[0], counter_1_q[2], counter_1_q[1]);
  LED led_4 (.in(not_4_out));
  LED led_5 (.in(and_5_out));
  LED led_6 (.in(and_3_out));
endmodule
